# Fritzing sketch garage (saved by Fritzing 0.9.2b)

parts:
  U1 = 2-Channel 5v Relay Shield [package=relay-2ch5v10a]
  Raspberry_Pi1 = Raspberry Pi 2
  S1 = Reed switch [package=THT]
  R1 = Resistor [tolerance=±5% resistance=10k package="0805 [SMD]"]

nets:
  VCC: U1.VCC, Raspberry_Pi1.5V
  GND: U1.GND, Raspberry_Pi1.GND, S1.pin_1
  N1: U1.IN1, Raspberry_Pi1.GPIO19
  N2: Raspberry_Pi1.GPIO16, R1.Pin_1

notes:
  To the garage door unit

custom parts:
  2-Channel 5v Relay Shield: 2 Channel 5v Relay Shield w. 2x SPD-06VDC-SD-C
